# Fritzing sketch 7segment-display (saved by Fritzing 0.9.3b)
breadboards: 1

parts:
  元件1 = Arduino Nano (Rev3.0)
  U1 = 7-SEGMENT-DISPLAY [package=7-segment-display]
  R1 = Resistor [tolerance=±5% resistance=220 package=THT]  # not connected
  S1 = Pushbutton [package="[THT]"]
  S2 = Pushbutton [package="[THT]"]
  R2 = Resistor [tolerance=±5% resistance=220 package=THT]
  R3 = Resistor [tolerance=±5% resistance=220 package=THT]
  LED1 = LED - 5mm [color="Green (555nm)" package="5 mm [THT]"]
  LED2 = LED - 5mm [color="Red (633nm)" package="5 mm [THT]"]
  R4 = Resistor [tolerance=±5% resistance=220 package=THT]
  DHT11_1 = DHT11 module  # not connected

nets:
  N1: 元件1.GND, S1.Pin_1, S1.Pin_2, S2.Pin_1, S2.Pin_2
  N2: 元件1.D2, U1.G2
  N3: 元件1.D3, U1.A
  N4: 元件1.D4, U1.DP
  N5: 元件1.D5, U1.G1
  N6: 元件1.D6, U1.D
  N7: 元件1.D7, U1.G
  N8: 元件1.D8, U1.E
  N9: 元件1.D11/MOSI, LED2.cathode
  N10: 元件1.D12/MISO, LED1.cathode
  N11: 元件1.5V, R2.Pin_1, R3.Pin_1, R4.Pin_1
  N12: 元件1.A3, S2.Pin_3, S2.Pin_4, R3.Pin_0
  N13: 元件1.A2, S1.Pin_3, S1.Pin_4, R2.Pin_0
  N14: LED1.anode, LED2.anode, R4.Pin_0

custom parts:
  DHT11 module: DHT11 black pcb module
